# Fritzing sketch LED-Matrix (saved by Fritzing 0.9.3b)

parts:
  Bauteil1 = Arduino Uno (Rev3)
  8x8_LED_Modul_mit_MAX1 = 8x8 LED Modul mit MAX7219 [package=THT]

nets:
  N1: Bauteil1.D11_PWM/MOSI, 8x8_LED_Modul_mit_MAX1.CLK_Eingang
  N2: Bauteil1.D12/MISO, 8x8_LED_Modul_mit_MAX1.CS_Eingang
  N3: Bauteil1.D13/SCK, 8x8_LED_Modul_mit_MAX1.DIN_Eingang
  N4: Bauteil1.5V, 8x8_LED_Modul_mit_MAX1.VCC_Eingang
  N5: Bauteil1.GND, 8x8_LED_Modul_mit_MAX1.GND_Eingang

notes:
  The upper left LED is at Position 0,0
